// Logisim project controlador_semaforos.circ as structural Verilog: 4 circuits, main circuit main
module main (
  input  S,
  input  B
);

  wire and_1_out, and_2_out, CLK_out, cont_7segm_1_a, cont_7segm_1_b, cont_7segm_1_c, cont_7segm_1_d,
       cont_7segm_1_e, cont_7segm_1_f, cont_7segm_1_g, not_1_out, not_2_out, not_3_out, not_4_out, or_1_out,
       peoes_1_p0, peoes_1_p1, peoes_1_rp1, peoes_1_rp2, veiculos_1_rv1, veiculos_1_v0, veiculos_1_v1;

  Clock CLK (.out(CLK_out));
  or or_1 (or_1_out, S, B);
  Veiculos veiculos_1 (
    .S_B(or_1_out), .RP1(peoes_1_rp1), .CLK(CLK_out), .V1(veiculos_1_v1), .V0(veiculos_1_v0),
    .RV1(veiculos_1_rv1));
  Peoes peoes_1 (
    .RV1(veiculos_1_rv1), .CLK(CLK_out), .RP2(peoes_1_rp2), .RP1(peoes_1_rp1), .P1(peoes_1_p1),
    .P0(peoes_1_p0));
  Cont_7Segm cont_7segm_1 (
    .RP2(peoes_1_rp2), .CLK(CLK_out), .a(cont_7segm_1_a), .b(cont_7segm_1_b), .c(cont_7segm_1_c),
    .d(cont_7segm_1_d), .e(cont_7segm_1_e), .f(cont_7segm_1_f), .g(cont_7segm_1_g));
  not not_1 (not_1_out, veiculos_1_v1);
  and and_1 (and_1_out, not_1_out, not_2_out);
  not not_2 (not_2_out, veiculos_1_v0);
  not not_3 (not_3_out, peoes_1_p1);
  and and_2 (and_2_out, not_3_out, not_4_out);
  not not_4 (not_4_out, peoes_1_p0);
  LED led_1 (.in(veiculos_1_v1));
  LED led_2 (.in(veiculos_1_v0));
  LED led_3 (.in(and_1_out));
  LED led_4 (.in(peoes_1_p1));
  LED led_5 (.in(peoes_1_p0));
  LED led_6 (.in(and_2_out));
  _7_Segment_Display u_7_segment_display_1 (
    .g(cont_7segm_1_a), .f(cont_7segm_1_b), .a(cont_7segm_1_c), .b(cont_7segm_1_d), .e(cont_7segm_1_e),
    .d(cont_7segm_1_f), .c(cont_7segm_1_g));  // open: dp

  // Notes on the sheet:
  //   Semáforo dos Veículos
  //   Semáforo dos Peões
endmodule

module Peoes (
  input  RV1,
  input  CLK,
  output RP2,
  output RP1,
  output P1,
  output P0
);

  wire and_1_out, and_2_out, and_3_out, nand_1_out, not_1_out, or_1_out, T0_q, T0_qn, T1_q, T1_qn, T2_q,
       T2_qn, T3_q, T3_qn;

  and and_1 (and_1_out, T2_q, T1_q, T0_q);
  not not_1 (not_1_out, RV1);
  and and_2 (and_2_out, T3_q, T1_q, T0_q);
  or or_1 (or_1_out, and_1_out, and_2_out);
  T_Flip_Flop T3 (.T(or_1_out), .clk(CLK), .Q(T3_q), .Qn(T3_qn));  // open: reset, preset
  and and_3 (and_3_out, T3_qn, T1_q, T0_q);
  T_Flip_Flop T2 (.T(and_3_out), .clk(CLK), .Q(T2_q), .Qn(T2_qn));  // open: reset, preset
  T_Flip_Flop T1 (.T(T0_q), .clk(CLK), .Q(T1_q), .Qn(T1_qn));  // open: reset, preset
  nand nand_1 (nand_1_out, T3_qn, T2_qn, T1_qn, T0_qn, not_1_out);
  T_Flip_Flop T0 (.T(nand_1_out), .clk(CLK), .Q(T0_q), .Qn(T0_qn));  // open: reset, preset
  and and_4 (P1, T3_qn, T2_qn, T1_qn);
  and and_5 (P0, T3_q, T1_q);
  and and_6 (RP2, T0_q, P1);
  and and_7 (RP1, T0_qn, P1);
endmodule

module Cont_7Segm (
  input  RP2,
  input  CLK,
  output a,
  output b,
  output c,
  output d,
  output e,
  output f,
  output g
);

  wire and_1_out, and_2_out, and_3_out, and_4_out, and_5_out, and_6_out, and_7_out, and_8_out, and_9_out,
       and_10_out, and_11_out, and_12_out, and_13_out, and_14_out, and_15_out, and_16_out, nand_1_out,
       or_1_out, or_2_out, or_3_out, T0_q, T0_qn, T1_q, T1_qn, T2_q, T2_qn, T3_q, T3_qn, xor_1_out;

  and and_1 (and_1_out, RP2, T2_qn, T1_qn, T0_qn);
  or or_1 (or_1_out, and_1_out, T3_q);
  T_Flip_Flop T3 (.T(or_1_out), .clk(CLK), .Q(T3_q), .Qn(T3_qn));  // open: reset, preset
  and and_2 (and_2_out, T2_q, T1_qn, T0_qn);
  or or_2 (or_2_out, and_2_out, T3_q);
  T_Flip_Flop T2 (.T(or_2_out), .clk(CLK), .Q(T2_q), .Qn(T2_qn));  // open: reset, preset
  and and_3 (and_3_out, T2_q, T0_qn);
  and and_4 (and_4_out, T1_q, T0_qn);
  or or_3 (or_3_out, and_3_out, T3_q, and_4_out);
  T_Flip_Flop T1 (.T(or_3_out), .clk(CLK), .Q(T1_q), .Qn(T1_qn));  // open: reset, preset
  nand nand_1 (nand_1_out, T3_qn, T2_qn, T1_qn, T0_qn);
  T_Flip_Flop T0 (.T(nand_1_out), .clk(CLK), .Q(T0_q), .Qn(T0_qn));  // open: reset, preset
  and and_5 (and_5_out, T2_q, T0_q);
  and and_6 (and_6_out, T1_q, T0_qn);
  and and_7 (and_7_out, T2_q, T1_qn);
  and and_8 (and_8_out, T2_q, T0_qn);
  or or_4 (c, and_5_out, T3_q, T1_q);
  or or_5 (e, and_6_out, T3_q);
  or or_6 (g, T3_q, T2_q, T0_q);
  xor xor_1 (xor_1_out, T2_q, T1_q);
  and and_9 (and_9_out, T1_q, T0_qn);
  or or_7 (b, and_7_out, T3_q, and_8_out);
  and and_10 (and_10_out, T2_qn, T0_q);
  and and_11 (and_11_out, T1_q, T0_q);
  and and_12 (and_12_out, T2_qn, T1_q);
  and and_13 (and_13_out, T2_q, T1_qn, T0_qn);
  and and_14 (and_14_out, T2_qn, T1_q);
  and and_15 (and_15_out, T1_q, T0_qn);
  and and_16 (and_16_out, T2_q, T1_qn, T0_q);
  or or_8 (a, xor_1_out, T3_q, and_9_out);
  or or_9 (d, and_10_out, and_11_out, T3_q, and_12_out, and_13_out);
  or or_10 (f, and_14_out, T3_q, and_15_out, and_16_out);

  // Notes on the sheet:
  //   x3
  //   x2
  //   x3
  //   x2
  //   x1
  //   x0
  //   x0
  //   x1
endmodule

module Veiculos (
  input  S_B,
  input  RP1,
  input  CLK,
  output V1,
  output V0,
  output RV1
);

  wire and_1_out, and_2_out, and_3_out, and_4_out, and_5_out, and_7_out, and_8_out, and_9_out, or_1_out,
       or_2_out, T0_q, T0_qn, T1_q, T1_qn, T2_q, T2_qn;

  and and_1 (and_1_out, T1_q, T0_q);
  and and_2 (and_2_out, T2_q, T0_q);
  or or_1 (or_1_out, and_2_out, and_1_out);
  T_Flip_Flop T2 (.T(or_1_out), .clk(CLK), .Q(T2_q), .Qn(T2_qn));  // open: reset, preset
  and and_3 (and_3_out, T2_qn, T0_q);
  T_Flip_Flop T1 (.T(and_3_out), .clk(CLK), .Q(T1_q), .Qn(T1_qn));  // open: reset, preset
  and and_4 (and_4_out, S_B, T2_qn);
  and and_5 (and_5_out, RP1, T2_q);
  or or_2 (or_2_out, and_4_out, T1_q, T0_q, and_5_out);
  T_Flip_Flop T0 (.T(or_2_out), .clk(CLK), .Q(T0_q), .Qn(T0_qn));  // open: reset, preset
  and and_6 (RV1, T2_qn, T1_q, T0_q);
  and and_7 (and_7_out, T2_qn, T1_qn, T0_q);
  and and_8 (and_8_out, T1_q, T0_qn);
  and and_9 (and_9_out, T1_q, T0_q);
  or or_3 (V0, and_7_out, and_8_out);
  or or_4 (V1, T2_q, and_9_out);
endmodule
